# Fritzing sketch Untitled Sketch (saved by Fritzing 0.9.3b)

parts:
  Part1 = Arduino Uno (Rev3) - ICSP
  Part2 = FC-28 Soil Hygrometer Module
  Part3 = FC-28 Soil Hygrometer Module - Probe
  KY-1 = Keyes Relay [package=THT]
  BAT1 = BC9VPC [package=bc9vpc]
  M1 = DC Motor  # not connected

nets:
  N1: Part1.A3, Part2.AO
  N2: Part1.D3_PWM, KY-1.ground
  N3: Part1.5V, KY-1.signal
  GND: Part1.GND, Part2.GND, KY-1.power
  VIN: Part1.VIN, Part2.VCC
  N4: Part2.POS, Part3.POS
  N5: Part2.NEG, Part3.NEG
  N6: KY-1.C, BAT1.V+

notes:
  5V DC Water pump
  5v - 12v relay module
  FC -28 Soil hydrometer

custom parts:
  FC-28 Soil Hygrometer Module: The FC-28 is a soil hygrometer module that uses the Texas Instruments LM393 comparator chip to provide an analog measurement of soil humidity. The digital output is high when soil moisture is over a certain threshold, as determined by adjusting the potentiometer.
  FC-28 Soil Hygrometer Module - Probe: The FC-28 is a soil hygrometer module that uses the Texas Instruments LM393 comparator chip to provide an analog measurement of soil humidity.
  Keyes Relay: The Keyes 5V relay module is suitable for SCM development, home appliance control. It uses a 5V~12V TIL control signal which can control DC / AC signal.
